# Fritzing sketch AVR_&_Shift_Register_Test (saved by Fritzing 0.9.2b)
breadboards: 2

parts:
  U1 = atmega168 [package=dip]
  U2 = mystery part, 16 pins [chip_label=SN74HC595]
  C1 = Ceramic Capacitor [capacitance=100nF package="100 mil [THT, multilayer]"]
  R1 = Resistor [tolerance=±5% resistance=10k package=THT]
  R2 = Resistor [tolerance=±5% resistance=1k package=THT]
  R3 = Resistor [tolerance=±5% resistance=1k package=THT]
  R4 = Resistor [tolerance=±5% resistance=1k package=THT]
  R5 = Resistor [tolerance=±5% resistance=1k package=THT]
  R6 = Resistor [tolerance=±5% resistance=1k package=THT]
  R7 = Resistor [tolerance=±5% resistance=1k package=THT]
  R8 = Resistor [tolerance=±5% resistance=1k package=THT]
  R9 = Resistor [tolerance=±5% resistance=1k package=THT]
  LED1 = LED - 3mm [color="Red (633nm)" package="3 mm [THT]"]
  LED2 = LED - 3mm [color="Red (633nm)" package="3 mm [THT]"]
  LED3 = LED - 3mm [color="Red (633nm)" package="3 mm [THT]"]
  LED4 = LED - 3mm [color="Red (633nm)" package="3 mm [THT]"]
  LED5 = LED - 3mm [color="Red (633nm)" package="3 mm [THT]"]
  LED6 = LED - 3mm [color="Red (633nm)" package="3 mm [THT]"]
  LED7 = LED - 3mm [color="Red (633nm)" package="3 mm [THT]"]
  LED8 = LED - 3mm [color="Red (633nm)" package="3 mm [THT]"]
  C2 = Ceramic Capacitor [capacitance=100nF package="100 mil [THT, multilayer]"]

nets:
  N1: U1.VCC, U2.pin16, C1.1, R1.Pin_0, C2.0
  N2: U1.GND#7, U2.pin8, U2.pin13, C1.0, LED1.cathode, LED2.cathode, LED3.cathode, LED4.cathode, LED5.cathode, LED6.cathode, LED7.cathode, LED8.cathode, C2.1
  N3: U1.D9_(PWM), U2.pin14
  N4: U1.D10_(PWM), U2.pin11
  N5: U1.D11_(PWM), U2.pin12
  N6: U2.pin1, R3.Pin_0
  N7: U2.pin2, R4.Pin_0
  N8: U2.pin3, R5.Pin_0
  N9: U2.pin4, R6.Pin_0
  N10: U2.pin5, R7.Pin_0
  N11: U2.pin6, R8.Pin_0
  N12: U2.pin7, R9.Pin_0
  N13: U2.pin10, R1.Pin_1
  N14: U2.pin15, R2.Pin_0
  N15: R2.Pin_1, LED1.anode
  N16: R3.Pin_1, LED2.anode
  N17: R4.Pin_1, LED3.anode
  N18: R5.Pin_1, LED4.anode
  N19: R6.Pin_1, LED5.anode
  N20: R7.Pin_1, LED6.anode
  N21: R8.Pin_1, LED7.anode
  N22: R9.Pin_1, LED8.anode
